# Fritzing sketch schematic (saved by Fritzing 0.9.3b)
breadboards: 1

parts:
  LED1 = smd LED [color="Red (633nm)" package="1206 [SMD]"]  # not connected
  LED2 = smd LED [color="Red (633nm)" package="1206 [SMD]"]
  R1 = Resistor [tolerance=±5% resistance=220 package="1206 [SMD]"]
  R2 = Resistor [tolerance=±5% resistance=220 package="1206 [SMD]"]
  U1 = ESP32-38PinWide [part_number=ESP32-38PinWide]

nets:
  N1: LED2.cathode, U1.GND
  N2: LED2.anode, R1.Pin_1
  N3: R1.Pin_0, U1.GPIO27
  N4: R2.Pin_0, U1.GPIO26

notes:
  GPIO:26
  GPIO:27

custom parts:
  ESP32-38PinWide: Generic 38-Pin ESP32 with wide format (only access to one side of pins on a breadboard) based on Stephen Lilley's HiLetgo ESP-WROOM-32 ESP32 ESP-32S Development Board.
